# Fritzing sketch CARRO BLUETOOTH (saved by Fritzing 0.9.9b)
breadboards: 1

parts:
  Componente2 = Arduino Uno (Rev3) - ICSP
  M1 = gear-motor
  M2 = gear-motor
  L298N1 = L298N DC motor driver
  BT1 = Bluetooth HC-06d [package=THT]
  BAT1 = BC9VPC [package=bc9vpc]  # not connected
  U1 = SWITCH-SPST-2 [package=r_sw_th]
  VCC2 = 4 x AAA Battery Mount

nets:
  N1: Componente2.D9_PWM, L298N1.IN4
  N2: Componente2.D10_PWM/SS, L298N1.IN3
  N3: Componente2.D11_PWM/MOSI, L298N1.IN2
  N4: Componente2.D12/MISO, L298N1.IN1
  N5: Componente2.D0/RX, BT1.TXD
  N6: Componente2.D1/TX, BT1.RXD
  5V: Componente2.5V, BT1.VCC
  GND: Componente2.GND, L298N1.GND, BT1.GND, VCC2.-
  N7: M1.pin_1, L298N1.OUT4
  N8: M1.pin_2, L298N1.OUT3
  N9: M2.pin_1, L298N1.OUT2
  N10: M2.pin_2, L298N1.OUT1
  N11: U1.O, U1.P, VCC2.+

custom parts:
  L298N DC motor driver: 2x DC motor driver with 78M05 positive voltage regulator (7..35 V) L298N: max 46 V, 2 A Set 5 V Enable jumper to enable 5 V regultor (needed for the L298N) and +5 V output at screw terminal or supply external +5 V at screw terminal Set ENA and/or ENB to +5 V to enable motor permanently or supply ENA and/or ENB with PWM signal IN1 and IN2 set rotation directory for motor A (OUT1/OUT2) IN2 and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
  Bluetooth HC-06d: Bluetooth HC-06 - face down, pins down 16.5mm x 37.5mm PCB
